// Logisim project simple_computer.circ as structural Verilog: 7 circuits, main circuit main
module main (
  input  STEP,
  input  in_2,
  input  [7:0] ADDR_IN_MAN,
  input  MANUAL_INPUT,
  input  [3:0] DATA_IN_MAN
);

  wire A_IN, A_OUT, ADDR_OUT, ALU_OUT, aluadd_1_cout, B_IN, B_OUT, button_1_out, C_EN, C_FLAG, C_OUT,
       clocklogic_1_clockout, H_IN, HALT, INSTR_IN, INV_CLOCK, JMP, L_IN, MEM_IN, OUT_EN, RD_MEM, SUB, WR_MEM;
  wire [3:0] A_q, aluadd_1_sum, B_q, controlled_buffer_1_out, controlled_buffer_2_out,
       controlled_buffer_3_out, controlled_buffer_6_out, controlled_buffer_7_out, controlled_buffer_8_out,
       controlled_buffer_11_out, H_q, INSTR, L_q, multiplexer_1_out, O_q, ram_1_dout, xor_1_out;
  wire [7:0] controlled_buffer_9_out, controlled_buffer_10_out, counter_1_q, MRA_q, multiplexer_2_out;

  Button button_1 (.out(button_1_out));
  assign controlled_buffer_1_out = A_IN ? controlled_buffer_3_out : 4'bz;  // Controlled_Buffer controlled_buffer_1
  assign controlled_buffer_2_out = B_IN ? controlled_buffer_3_out : 4'bz;  // Controlled_Buffer controlled_buffer_2
  assign xor_1_out = B_q ^ {4{SUB}};  // XOR_Gate xor_1, 4 bits wide
  Register #(.width(4)) A (.D(controlled_buffer_1_out), .en(A_IN), .clk(clocklogic_1_clockout), .Q(A_q), .clr(in_2));
  Register #(.width(4)) B (.D(controlled_buffer_2_out), .en(B_IN), .clk(clocklogic_1_clockout), .Q(B_q), .clr(in_2));
  clocklogic clocklogic_1 (.Mode(STEP), .Step(button_1_out), .Halt(HALT), .ClockOut(clocklogic_1_clockout));
  aluadd aluadd_1 (.CIN(SUB), .A(A_q), .B(xor_1_out), .SUM(aluadd_1_sum), .COUT(aluadd_1_cout));
  not not_1 (INV_CLOCK, clocklogic_1_clockout);
  assign controlled_buffer_3_out = A_OUT ? A_q : 4'bz;  // Controlled_Buffer controlled_buffer_3
  assign controlled_buffer_3_out = B_OUT ? B_q : 4'bz;  // Controlled_Buffer controlled_buffer_4
  assign controlled_buffer_3_out = ALU_OUT ? aluadd_1_sum : 4'bz;  // Controlled_Buffer controlled_buffer_5
  command command_1 (
    .RESET(in_2), .C_FLAG(C_FLAG), .INSTR_DATA(INSTR), .CLOCK(INV_CLOCK), .HALT(HALT), .A_IN(A_IN),
    .A_OUT(A_OUT), .B_IN(B_IN), .B_OUT(B_OUT), .ALU_OUT(ALU_OUT), .SUB(SUB), .JMP(JMP), .ADDR_OUT(ADDR_OUT),
    .C_EN(C_EN), .C_OUT(C_OUT), .WR_MEM(WR_MEM), .RD_MEM(RD_MEM), .MEM_IN(MEM_IN), .L_IN(L_IN), .H_IN(H_IN),
    .OUT_EN(OUT_EN), .INSTR_IN(INSTR_IN));
  Register #(.width(4)) O (.D(controlled_buffer_3_out), .en(OUT_EN), .clk(clocklogic_1_clockout), .Q(O_q), .clr(in_2));
  assign controlled_buffer_6_out = INSTR_IN ? controlled_buffer_3_out : 4'bz;  // Controlled_Buffer controlled_buffer_6
  Hex_Digit_Display hex_digit_display_1 (.value(O_q));  // open: dp
  xor xor_2 (C_FLAG, SUB, aluadd_1_cout);
  Register #(.width(4)) u_INSTR (
    .D(controlled_buffer_6_out), .en(INSTR_IN), .clk(clocklogic_1_clockout), .Q(INSTR), .clr(in_2));
  DotMatrix #(.matrixcols(4), .matrixrows(1)) dotmatrix_1 (.col0(O_q[3]), .col1(O_q[2]), .col2(O_q[1]), .col3(O_q[0]));
  assign controlled_buffer_7_out = L_IN ? controlled_buffer_3_out : 4'bz;  // Controlled_Buffer controlled_buffer_7
  assign controlled_buffer_8_out = H_IN ? controlled_buffer_3_out : 4'bz;  // Controlled_Buffer controlled_buffer_8
  Register #(.width(4)) L (.D(controlled_buffer_7_out), .en(L_IN), .clk(clocklogic_1_clockout), .Q(L_q), .clr(in_2));
  Register #(.width(4)) H (.D(controlled_buffer_8_out), .en(H_IN), .clk(clocklogic_1_clockout), .Q(H_q), .clr(in_2));
  RAM #(.asyncread("true"), .dataWidth(4)) ram_1 (
    .addr(multiplexer_2_out), .we(WR_MEM), .oe(RD_MEM), .clk(clocklogic_1_clockout), .din(multiplexer_1_out),
    .dout(ram_1_dout));
  Multiplexer #(.width(4)) multiplexer_1 (
    .in0(controlled_buffer_11_out), .in1(DATA_IN_MAN), .out(multiplexer_1_out), .sel(MANUAL_INPUT));
  Multiplexer #(.width(8)) multiplexer_2 (.in0(MRA_q), .in1(ADDR_IN_MAN), .out(multiplexer_2_out), .sel(MANUAL_INPUT));
  Counter counter_1 (
    .clr(in_2), .load(JMP), .up(1'b1), .count(C_EN), .clk(clocklogic_1_clockout),
    .D(controlled_buffer_9_out), .Q(counter_1_q));  // open: carry
  assign controlled_buffer_9_out = JMP ? {H_q, L_q} : 8'bz;  // Controlled_Buffer controlled_buffer_9
  assign controlled_buffer_10_out = ADDR_OUT ? {H_q, L_q} : 8'bz;  // Controlled_Buffer controlled_buffer_10
  assign controlled_buffer_11_out = WR_MEM ? controlled_buffer_3_out : 4'bz;  // Controlled_Buffer controlled_buffer_11
  assign controlled_buffer_3_out = RD_MEM ? ram_1_dout : 4'bz;  // Controlled_Buffer controlled_buffer_12
  assign controlled_buffer_10_out = C_OUT ? counter_1_q : 8'bz;  // Controlled_Buffer controlled_buffer_13
  Register MRA (.D(controlled_buffer_10_out), .en(MEM_IN), .clk(clocklogic_1_clockout), .Q(MRA_q), .clr(in_2));

  // Other names for the same wires on the sheet: C_CLEAR = in_2

  // Notes on the sheet:
  //   4bit DATA BUS
  //   8bit ADDRESS BUS
endmodule

module clocklogic (
  input  Mode,
  input  Step,
  input  Halt,
  output ClockOut
);

  wire and_1_out, and_2_out, ClockIn_out, not_1_out, not_2_out, or_1_out;

  Clock ClockIn (.out(ClockIn_out));
  not not_1 (not_1_out, Mode);
  and and_1 (and_1_out, ClockIn_out, Mode);
  and and_2 (and_2_out, not_1_out, Step);
  or or_1 (or_1_out, and_1_out, and_2_out);
  not not_2 (not_2_out, Halt);
  and and_3 (ClockOut, or_1_out, not_2_out);
endmodule

module fulladd (
  input  A,
  input  B,
  input  CIN,
  output SUM,
  output COUT
);

  wire and_1_out, and_2_out, xor_1_out;

  xor xor_1 (xor_1_out, A, B);
  and and_1 (and_1_out, A, B);
  and and_2 (and_2_out, xor_1_out, CIN);
  xor xor_2 (SUM, xor_1_out, CIN);
  or or_1 (COUT, and_2_out, and_1_out);
endmodule

module aluadd (
  input  CIN,
  input  [3:0] A,
  input  [3:0] B,
  output [3:0] SUM,
  output COUT
);

  wire fulladd_1_cout, fulladd_2_cout, fulladd_3_cout;

  fulladd fulladd_1 (.A(A[0]), .B(B[0]), .CIN(CIN), .SUM(SUM[0]), .COUT(fulladd_1_cout));
  fulladd fulladd_2 (.A(A[1]), .B(B[1]), .CIN(fulladd_1_cout), .SUM(SUM[1]), .COUT(fulladd_2_cout));
  fulladd fulladd_3 (.A(A[2]), .B(B[2]), .CIN(fulladd_2_cout), .SUM(SUM[2]), .COUT(fulladd_3_cout));
  fulladd fulladd_4 (.A(A[3]), .B(B[3]), .CIN(fulladd_3_cout), .SUM(SUM[3]), .COUT(COUT));
endmodule

module fullsub (
  input  A,
  input  B,
  input  CIN,
  output DIFF,
  output COUT
);

  wire and_1_out, and_2_out, not_1_out, not_2_out, xor_1_out;

  not not_1 (not_1_out, A);
  xor xor_1 (xor_1_out, A, B);
  not not_2 (not_2_out, xor_1_out);
  and and_1 (and_1_out, not_1_out, B);
  xor xor_2 (DIFF, xor_1_out, CIN);
  and and_2 (and_2_out, CIN, not_2_out);
  or or_1 (COUT, and_2_out, and_1_out);
endmodule

module alusub (
  input  [3:0] A,
  input  [3:0] B,
  output [3:0] DIFF,
  output COUT
);

  wire fullsub_1_cout, fullsub_2_cout, fullsub_3_cout;

  fullsub fullsub_1 (.A(A[0]), .B(B[0]), .DIFF(DIFF[0]), .COUT(fullsub_1_cout));  // open: CIN
  fullsub fullsub_2 (.A(A[1]), .B(B[1]), .CIN(fullsub_1_cout), .DIFF(DIFF[1]), .COUT(fullsub_2_cout));
  fullsub fullsub_3 (.A(A[2]), .B(B[2]), .CIN(fullsub_2_cout), .DIFF(DIFF[2]), .COUT(fullsub_3_cout));
  fullsub fullsub_4 (.A(A[3]), .B(B[3]), .CIN(fullsub_3_cout), .DIFF(DIFF[3]), .COUT(COUT));
endmodule

module command (
  input  RESET,
  input  C_FLAG,
  input  [3:0] INSTR_DATA,
  input  CLOCK,
  output HALT,
  output A_IN,
  output A_OUT,
  output B_IN,
  output B_OUT,
  output ALU_OUT,
  output SUB,
  output JMP,
  output ADDR_OUT,
  output C_EN,
  output C_OUT,
  output WR_MEM,
  output RD_MEM,
  output MEM_IN,
  output L_IN,
  output H_IN,
  output OUT_EN,
  output INSTR_IN
);

  wire or_1_out;
  wire [3:0] counter_1_q;
  wire [5:0] rom_3_data;

  or or_1 (or_1_out, rom_3_data[0], RESET);
  Counter #(.max('hf), .width(4)) counter_1 (
    .clr(or_1_out), .up(1'b1), .count(1'b1), .clk(CLOCK), .Q(counter_1_q));  // open: load, D, carry
  ROM rom_1 (.addr({INSTR_DATA, counter_1_q}), .data({A_IN, A_OUT, B_IN, B_OUT, H_IN, L_IN, ALU_OUT, SUB}));
  ROM rom_2 (.addr({INSTR_DATA, counter_1_q}), .data({JMP, C_EN, C_OUT, MEM_IN, ADDR_OUT, WR_MEM, RD_MEM, INSTR_IN}));
  ROM rom_3 (.addr({INSTR_DATA, counter_1_q}), .data({OUT_EN, HALT, rom_3_data}));

  // Other names for the same wires on the sheet: INSTR[3:0] = INSTR_DATA; C_CLEAR = RESET

  // Notes on the sheet:
  //   contents of rom_1 (hex, n*v repeats v):
  //   35*0 8 0 4 0 80 11*0 80 15*0 8 0 4 0 20 11*0 20 15*0 8 0 4 0 20 82 10*0 20 82 14*0 8 0 4 0 20 83
  //   10*0 20 83 93*0 40
  //   contents of rom_2 (hex, n*v repeats v):
  //   30 43 14*0 30 43 14*0 30 43 30 42 30 42 18 2 8*0 30 43 30 42 12*0 30 43 30 42 30 42 18 2 8*0 30 43
  //   30 42 12*0 30 43 30 42 30 42 18 2 8*0 30 43 30 42 12*0 30 43 30 42 30 42 18 2 8*0 30 43 30 42 12*0
  //   30 43 14*0 30 43 14*0 30 43 14*0 30 43 14*0 30 43 14*0 30 43
  //   contents of rom_3 (hex, n*v repeats v):
  //   0 0 1 15*0 1 21*0 1 11*0 1 19*0 1 11*0 1 20*0 1 11*0 1 19*0 1 11*0 1 74*0 40 17*0 80 1
  //   if less than 8 operations, return counter to 0 so we don't loose machine cycles
endmodule
